# Fritzing sketch Schaltung (saved by Fritzing 1.0.3b)
circuit board: 8.46667cm x 5.64444cm
breadboards: 1

parts:
  LCM1602_IIC1 = LCM1602 IIC [part_number="LCM1602 IIC" chip_label="LCM1602 IIC" package="DIP (Dual Inline) [THT]"]
  R1_(10k) = Resistor [tolerance=±5% power=0.25W resistance=10k package=THT]
  R2_(10k) = Resistor [tolerance=±5% power=0.25W resistance=10k package=THT]
  Display = male pin header, 4 pins [form="♂ (male)"]
  4x20_LCD_screen_w/Red_Screen1 = 4x20 LCD screen w/Red Screen
  Arduino_Nano = Arduino Nano (Rev3.0) (ICSP)
  S2 = Pushbutton [package="[THT]"]
  S1 = Pushbutton [package="[THT]"]

nets:
  VSS: LCM1602_IIC1.VSS, 4x20_LCD_screen_w/Red_Screen1.VSS
  VDD: LCM1602_IIC1.VDD, 4x20_LCD_screen_w/Red_Screen1.VDD
  N1: LCM1602_IIC1.V0, 4x20_LCD_screen_w/Red_Screen1.V0
  N2: LCM1602_IIC1.RS, 4x20_LCD_screen_w/Red_Screen1.RS
  N3: LCM1602_IIC1.RW, 4x20_LCD_screen_w/Red_Screen1.R/W
  N4: LCM1602_IIC1.E, 4x20_LCD_screen_w/Red_Screen1.E
  N5: LCM1602_IIC1.D0, 4x20_LCD_screen_w/Red_Screen1.DB0
  N6: LCM1602_IIC1.D1, 4x20_LCD_screen_w/Red_Screen1.DB1
  N7: LCM1602_IIC1.D2, 4x20_LCD_screen_w/Red_Screen1.DB2
  N8: LCM1602_IIC1.D3, 4x20_LCD_screen_w/Red_Screen1.DB3
  N9: LCM1602_IIC1.D4, 4x20_LCD_screen_w/Red_Screen1.DB4
  N10: LCM1602_IIC1.D5, 4x20_LCD_screen_w/Red_Screen1.DB5
  N11: LCM1602_IIC1.D6, 4x20_LCD_screen_w/Red_Screen1.DB6
  N12: LCM1602_IIC1.D7, 4x20_LCD_screen_w/Red_Screen1.DB7
  N13: LCM1602_IIC1.A, 4x20_LCD_screen_w/Red_Screen1.LED+
  N14: LCM1602_IIC1.K, 4x20_LCD_screen_w/Red_Screen1.LED-
  GND: LCM1602_IIC1.GND, R1_(10k).Pin_0, R2_(10k).Pin_0, Display.pin1, Arduino_Nano.GND
  VCC: LCM1602_IIC1.VCC, Display.pin2, Arduino_Nano.VIN, S2.Pin_1, S2.Pin_2, S1.Pin_1, S1.Pin_2
  N15: LCM1602_IIC1.SDA, Display.pin3, Arduino_Nano.A4
  N16: LCM1602_IIC1.SCL, Display.pin4, Arduino_Nano.A5
  N17: R1_(10k).Pin_1, Arduino_Nano.D2, S1.Pin_3, S1.Pin_4
  N18: R2_(10k).Pin_1, Arduino_Nano.D3, S2.Pin_3, S2.Pin_4

notes:
  2024 Johanna & Marc

custom parts:
  LCM1602 IIC: I2C-Module to use a 1602 or 2004 LCD on with the wire.h libory Serial LCD Modul
  4x20 LCD screen w/Red Screen: A standard character display with 4x20 characters.
